// Logisim project OffBrandARMCPU.circ as structural Verilog: 2 circuits, main circuit main
module main (
  output [7:0] out_1,
  output [7:0] out_2,
  output [7:0] instruction,
  output ReadMem,
  output WriteMem,
  output ALUOp,
  output [7:0] RegData1,
  output [1:0] WriteReg,
  output [1:0] ReadReg1,
  output RegWrite,
  output [7:0] RegData2,
  output [1:0] ReadReg2,
  output [7:0] RegDataW
);

  wire and_1_out, and_2_out, and_3_out, and_4_out, clock_1_out, decoder_1_out0, decoder_1_out1,
       decoder_1_out2, decoder_1_out3;
  wire [3:0] alu_1_aluoutput, alu_1_aluoutput_2;
  wire [7:0] DataMemory_dout, undriven, X0_q, X1_q, X2_q, X3_q;

  Register PC (.D(out_2), .en(1'b1), .clk(clock_1_out), .Q(out_1));  // open: clr
  Clock clock_1 (.out(clock_1_out));
  Decoder #(.select(2)) decoder_1 (
    .out0(decoder_1_out0), .out1(decoder_1_out1), .out2(decoder_1_out2), .out3(decoder_1_out3),
    .sel(instruction[5:4]));  // open: en
  Adder adder_1 (.a(8'h1), .b(out_1), .out(out_2));  // open: cin, cout
  RAM #(.enables("line")) InstructionMemory (
    .addr(out_1), .we(1'b0), .oe(1'b1), .clk(clock_1_out), .din(undriven), .dout(instruction));
  and and_1 (and_1_out, decoder_1_out0, RegWrite);
  and and_2 (and_2_out, decoder_1_out1, RegWrite);
  and and_3 (and_3_out, decoder_1_out2, RegWrite);
  and and_4 (and_4_out, decoder_1_out3, RegWrite);
  Register X0 (.D(RegDataW), .en(and_1_out), .clk(clock_1_out), .Q(X0_q));  // open: clr
  Register X1 (.D(RegDataW), .en(and_2_out), .clk(clock_1_out), .Q(X1_q));  // open: clr
  Register X2 (.D(RegDataW), .en(and_3_out), .clk(clock_1_out), .Q(X2_q));  // open: clr
  Register X3 (.D(RegDataW), .en(and_4_out), .clk(clock_1_out), .Q(X3_q));  // open: clr
  Multiplexer #(.select(2), .width(8)) multiplexer_1 (
    .in0(X0_q), .in1(X1_q), .in2(X2_q), .in3(X3_q), .out(RegData1), .sel(instruction[1:0]));
  Multiplexer #(.select(2), .width(8)) multiplexer_2 (
    .in0(X0_q), .in1(X1_q), .in2(X2_q), .in3(X3_q), .out(RegData2), .sel(instruction[3:2]));
  Multiplexer #(.select(2), .width(4)) multiplexer_3 (
    .in0(4'b1000), .in1(4'b1001), .in2(4'b1100), .in3(4'b0010), .out({RegWrite, ReadMem, WriteMem, ALUOp}),
    .sel(instruction[7:6]));
  ALU alu_1 (.RegData2(RegData2), .RegData1(RegData1), .ALUOp(ALUOp), .ALUOutput({alu_1_aluoutput_2, alu_1_aluoutput}));
  Hex_Digit_Display hex_digit_display_1 (.value(alu_1_aluoutput_2));  // open: dp
  Hex_Digit_Display hex_digit_display_2 (.value(alu_1_aluoutput));  // open: dp
  RAM #(.enables("line")) DataMemory (
    .addr({alu_1_aluoutput_2, alu_1_aluoutput}), .we(WriteMem), .oe(ReadMem), .clk(clock_1_out),
    .din({alu_1_aluoutput_2, alu_1_aluoutput}), .dout(DataMemory_dout));
  Multiplexer #(.width(8)) multiplexer_4 (
    .in0({alu_1_aluoutput_2, alu_1_aluoutput}), .in1(DataMemory_dout), .out(RegDataW), .sel(ReadMem));

  assign ReadReg1 = instruction[1:0];
  assign ReadReg2 = instruction[3:2];
  assign WriteReg = instruction[5:4];

  // Notes on the sheet:
  //   IF
  //   WriteReg: Which register to store the result
  //   InstructionMemory
  //   ReadReg1: This selects the first register to read. ReadReg2: This selects the second register to read.
  //   NextPC
  //   STRFlags
  //   LDRFlags
  //   ADDFlags
  //   SUBFlags
  //   ReadWrite: true (1) or false (0), write to a register 
  //   Anthony Eryan
  //   OffBrandARM CPU 
  //   I pledge my honor that I have abided by the Stevens Honor System.
  //   STR
  //   LDR
  //   ADD
  //   SUB
  //   Bit 3: WriteReg Bit 2: ReadMem Bit 1: WriteMem Bit 0: ALUOp
  //   ID
  //   EX
  //   (Hex) ALUOutput =
  //   ALUout  = computes memory address OR arithmetic on register values
  //   ME
  //   DataMemory
  //   WB
  //   Write back LDR (ReadMem = 1) , or ADD/SUB (ReadMem = 0)
endmodule

module ALU (
  input  [7:0] RegData2,
  input  [7:0] RegData1,
  input  ALUOp,
  output [7:0] ALUOutput
);

  wire [7:0] adder_1_out, subtractor_1_out;

  Adder adder_1 (.a(RegData2), .b(RegData1), .out(adder_1_out));  // open: cin, cout
  Subtractor subtractor_1 (.a(RegData2), .b(RegData1), .out(subtractor_1_out));  // open: bin, bout
  Multiplexer #(.width(8)) multiplexer_1 (.in0(adder_1_out), .in1(subtractor_1_out), .out(ALUOutput), .sel(ALUOp));
endmodule
